// Logisim project Single_Cycle_CPU.circ as structural Verilog: 7 circuits, main circuit Display
module main (
);

  wire ALUSrc, call, CLK, HLT, I_type, KBRead, MemWrite, out, put, RegWrite, ret, undriven;
  wire [1:0] RegDataSrc;
  wire [2:0] ALUOp, rd, rs, rt;
  wire [3:0] display_1_out_4, display_1_out_5, display_1_out_6, display_1_out_7, PCSrc;
  wire [6:0] KBOut;
  wire [15:0] ALU, bit_extender_1_out, data, imm, multiplexer_1_out, multiplexer_2_out, PC, ra, rs_out,
       rt_out;
  wire [19:0] inst;

  Clock clock_1 (.out(CLK));
  Return_Stack return_stack_1 (.CLK(CLK), .call(call), .ret(ret), .PC(PC), .Return_Address(ra));
  Program_Counter program_counter_1 (
    .sxt_imm8(imm), .rs(rs_out), .imm16(imm), .sp_1(ra), .HALT(HLT), .CLK(CLK), .PCSrc(PCSrc), .PC_out(PC));
  LED HALT (.in(HLT));
  Display display_1 (
    .Data(rs_out), .Enable(put), .CLK(CLK), .out_4(display_1_out_4), .out_5(display_1_out_5),
    .out_6(display_1_out_6), .out_7(display_1_out_7));
  ROM #(.addrWidth(16), .dataWidth(20)) rom_1 (.addr(PC), .data(inst));  // open: sel
  Hex_Digit_Display hex_digit_display_1 (.value(display_1_out_5));  // open: dp
  Hex_Digit_Display hex_digit_display_2 (.value(display_1_out_4));  // open: dp
  Hex_Digit_Display hex_digit_display_3 (.value(display_1_out_6), .dp(undriven));
  Hex_Digit_Display hex_digit_display_4 (.value(display_1_out_7));  // open: dp
  Hex_Digit_Display hex_digit_display_5 (.value(display_1_out_6), .dp(undriven));
  assign bit_extender_1_out = {{9{1'b0}}, KBOut};  // Bit_Extender bit_extender_1
  Control control_1 (
    .Instruction(inst), .put(put), .ALUOp(ALUOp), .out_7(rs), .out_8(rt), .out_10(rd), .MemWrite(MemWrite),
    .imm(imm), .PCSrc(PCSrc), .RegDataSrc(RegDataSrc), .RegWrite(RegWrite), .HALT(HLT), .ret(ret),
    .call(call), .I_type(I_type), .ALUSrc(ALUSrc), .rs_out(rs_out), .rt_out(rt_out), .KBRead(KBRead),
    .out(out));
  Multiplexer #(.select(2), .width(16)) multiplexer_1 (
    .in0(ALU), .in1(data), .in2(imm), .in3(bit_extender_1_out), .out(multiplexer_1_out), .sel(RegDataSrc));  // open: en
  TTY tty_1 (.data(rs_out[6:0]), .clk(CLK), .we(out));  // open: clr
  Keyboard keyboard_1 (.clk(CLK), .re(KBRead), .data(KBOut));  // open: clr, avail
  Register_File register_file_1 (
    .Data(multiplexer_1_out), .Enable(RegWrite), .I_type(I_type), .rd(rd), .rt(rt), .rs(rs), .CLK(CLK),
    .rs_out(rs_out), .rt_out(rt_out));
  Multiplexer #(.width(16)) multiplexer_2 (.in0(rt_out), .in1(imm), .out(multiplexer_2_out), .sel(ALUSrc));  // open: en
  ALU alu_1 (.A(rs_out), .B(multiplexer_2_out), .Op(ALUOp), .Output(ALU));
  RAM #(.addrWidth(16), .dataWidth(16), .bus("separate")) ram_1 (
    .addr(ALU), .din(rt_out), .data(data), .str(MemWrite), .clk(CLK));  // open: sel, ld, clr

  // Notes on the sheet:
  //   Instruction Memory
  //   Data Memory
  //   ALU
endmodule

module Display (
  input  [15:0] Data,
  input  Enable,
  input  CLK,
  output [3:0] out_4,
  output [3:0] out_5,
  output [3:0] out_6,
  output [3:0] out_7
);

  Register #(.width(16)) register_1 (.D(Data), .en(Enable), .Q({out_4, out_5, out_6, out_7}), .clk(CLK));  // open: clr
endmodule

module ALU (
  input  [15:0] A,
  input  [15:0] B,
  input  [2:0] Op,
  output [15:0] Output
);

  wire [15:0] A___B, A___B_t, nB, tunnel, tunnel_t, tunnel_t_t, tunnel_t_t_t;

  Adder #(.width(16)) adder_1 (.a(A), .b(B), .out(tunnel));  // open: cin, cout
  Shifter #(.width(16), .shift("lr")) shifter_1 (.in(A), .\dist (B[3:0]), .out(tunnel_t_t));
  assign A___B_t = A | B;  // OR_Gate or_1, 16 bits wide
  Subtractor #(.width(16)) subtractor_1 (.a(A), .b(B), .out(tunnel_t));  // open: bin, bout
  Shifter #(.width(16)) shifter_2 (.in(A), .\dist (B[3:0]), .out(tunnel_t_t_t));
  // NOT_Gate not_1 has open pins: in=open, out=nB
  assign A___B = A & B;  // AND_Gate and_1, 16 bits wide
  Multiplexer #(.select(3), .width(16)) multiplexer_1 (
    .in0({16{1'b0}}), .in1(tunnel), .in2(tunnel_t), .in3(A___B), .in4(A___B_t), .in5(nB), .in6(tunnel_t_t_t),
    .in7(tunnel_t_t), .out(Output), .sel(Op));  // open: en

  // Notes on the sheet:
  //   1 - Add
  //   2 - Subtract
  //   3 - AND
  //   4 - OR
  //   5 - Not
  //   6 - Shift Logical Left
  //   7 - Shift Logical Right
endmodule

module Register_File (
  input  [15:0] Data,
  input  Enable,
  input  I_type,
  input  [2:0] rd,
  input  [2:0] rt,
  input  [2:0] rs,
  input  CLK,
  output [15:0] rs_out,
  output [15:0] rt_out
);

  wire demultiplexer_1_out1, demultiplexer_1_out2, demultiplexer_1_out3, demultiplexer_1_out4,
       demultiplexer_1_out5, demultiplexer_1_out6, demultiplexer_1_out7;
  wire [2:0] multiplexer_1_out;
  wire [15:0] r1_q, r2_q, r3_q, r4_q, r5_q, r6_q, r7_q;

  Demultiplexer #(.select(3)) demultiplexer_1 (
    .out1(demultiplexer_1_out1), .out2(demultiplexer_1_out2), .out3(demultiplexer_1_out3),
    .out4(demultiplexer_1_out4), .out5(demultiplexer_1_out5), .out6(demultiplexer_1_out6),
    .out7(demultiplexer_1_out7), .in(Enable), .sel(multiplexer_1_out));  // open: out0, en
  Multiplexer #(.width(3)) multiplexer_1 (.in0(rd), .in1(rt), .out(multiplexer_1_out), .sel(I_type));  // open: en
  Register #(.width(16)) r1 (.D(Data), .en(demultiplexer_1_out1), .Q(r1_q), .clk(CLK));  // open: clr
  Register #(.width(16)) r2 (.D(Data), .en(demultiplexer_1_out2), .Q(r2_q), .clk(CLK));  // open: clr
  Register #(.width(16)) r3 (.D(Data), .en(demultiplexer_1_out3), .Q(r3_q), .clk(CLK));  // open: clr
  Register #(.width(16)) r4 (.D(Data), .en(demultiplexer_1_out4), .Q(r4_q), .clk(CLK));  // open: clr
  Register #(.width(16)) r5 (.D(Data), .en(demultiplexer_1_out5), .Q(r5_q), .clk(CLK));  // open: clr
  Register #(.width(16)) r6 (.D(Data), .en(demultiplexer_1_out6), .Q(r6_q), .clk(CLK));  // open: clr
  Register #(.width(16)) r7 (.D(Data), .en(demultiplexer_1_out7), .Q(r7_q), .clk(CLK));  // open: clr
  Multiplexer #(.select(3), .width(16)) multiplexer_2 (
    .in0({16{1'b0}}), .in1(r1_q), .in2(r2_q), .in3(r3_q), .in4(r4_q), .in5(r5_q), .in6(r6_q), .in7(r7_q),
    .out(rs_out), .sel(rs));  // open: en
  Multiplexer #(.select(3), .width(16)) multiplexer_3 (
    .in0({16{1'b0}}), .in1(r1_q), .in2(r2_q), .in3(r3_q), .in4(r4_q), .in5(r5_q), .in6(r6_q), .in7(r7_q),
    .out(rt_out), .sel(rt));  // open: en

  // Notes on the sheet:
  //   After the zero register, the inputs are r1-r7 from top to bottom for both muxes
endmodule

// RS
module Return_Stack (
  input  CLK,
  input  call,
  input  ret,
  input  [15:0] PC,
  output [15:0] Return_Address
);

  wire xor_1_out;
  wire [7:0] adder_1_out, multiplexer_1_out, multiplexer_2_out, sp_1, sp_q;
  wire [15:0] adder_2_out;

  Subtractor subtractor_1 (.a(sp_q), .b(8'h1), .out(sp_1));  // open: bin, bout
  Adder adder_1 (.a(sp_q), .b(8'h1), .out(adder_1_out));  // open: cin, cout
  Multiplexer #(.width(8)) multiplexer_1 (
    .in0(sp_1), .in1(adder_1_out), .out(multiplexer_1_out), .sel(call));  // open: en
  xor xor_1 (xor_1_out, call, ret);
  Register sp (.D(multiplexer_1_out), .en(xor_1_out), .Q(sp_q), .clk(CLK));  // open: clr
  Multiplexer #(.width(8)) multiplexer_2 (.in0(sp_q), .in1(sp_1), .out(multiplexer_2_out), .sel(ret));  // open: en
  Adder #(.width(16)) adder_2 (.a(16'h1), .b(PC), .out(adder_2_out));  // open: cin, cout
  RAM #(.dataWidth(16), .bus("separate")) ram_1 (
    .addr(multiplexer_2_out), .din(adder_2_out), .data(Return_Address), .str(call), .clk(CLK));  // open: sel, ld, clr
endmodule

// PC
module Program_Counter (
  input  HALT,
  input  [15:0] sxt_imm8,
  input  [15:0] rs,
  input  [15:0] imm16,
  input  [15:0] sp_1,
  input  CLK,
  input  [3:0] PCSrc,
  output [15:0] PC_out
);

  wire not_1_out;
  wire [15:0] adder_1_out, adder_2_out, multiplexer_1_out;

  Adder #(.width(16)) adder_1 (.a(PC_out), .b(16'h1), .out(adder_1_out));  // open: cin, cout
  Adder #(.width(16)) adder_2 (.a(PC_out), .b(sxt_imm8), .out(adder_2_out));  // open: cin, cout
  Multiplexer #(.select(4), .width(16)) multiplexer_1 (
    .in0(adder_1_out), .in1(adder_2_out), .in2(adder_2_out), .in3(adder_2_out), .in4(adder_2_out),
    .in5(adder_2_out), .in6(adder_2_out), .in7(rs), .in8(imm16), .in9(sp_1), .out(multiplexer_1_out),
    .sel(PCSrc));  // open: in10, in11, in12, in13, in14, in15, en
  Register #(.width(16)) PC (.D(multiplexer_1_out), .en(not_1_out), .Q(PC_out), .clk(CLK));  // open: clr
  // NOT_Gate not_1 has open pins: in=open, out=not_1_out

  // Other names for the same wires on the sheet: HLT = HALT; PC[15:0] = PC_out
endmodule

module Control (
  input  [19:0] Instruction,
  input  [15:0] rs_out,
  input  [15:0] rt_out,
  output put,
  output HALT,
  output [2:0] ALUOp,
  output [2:0] out_7,
  output [2:0] out_8,
  output ret,
  output [2:0] out_10,
  output MemWrite,
  output out,
  output KBRead,
  output [15:0] imm,
  output call,
  output [3:0] PCSrc,
  output [1:0] RegDataSrc,
  output RegWrite,
  output I_type,
  output ALUSrc
);

  wire _0, add, adi, \and , and_1_out, and_2_out, and_3_out, and_4_out, and_5_out, and_6_out, ani, beq, bez,
       bge, blt, bne, bnz, j, jr, ld, li, load, lui, \not , not_1_out, not_2_out, not_3_out, not_4_out, \or ,
       or_1_out, or_2_out, or_3_out, or_4_out, or_8_out, or_9_out, or_10_out, or_11_out, or_12_out,
       or_13_out, or_14_out, or_17_out, or_18_out, ori, sbi, shl, shr, sli, sri, sub, tunnel, tunnel_t,
       WrtFromALU;
  wire [2:0] priority_encoder_1_out;
  wire [15:0] bit_extender_1_out, bit_extender_2_out, bit_extender_3_out, bit_extender_4_out, shifter_1_out;

  assign bit_extender_1_out = {{8{1'b0}}, Instruction[7:0]};  // Bit_Extender bit_extender_1
  assign bit_extender_2_out = {{8{Instruction[7]}}, Instruction[7:0]};  // Bit_Extender bit_extender_2
  assign bit_extender_3_out = {{11{1'b0}}, Instruction[4:0]};  // Bit_Extender bit_extender_3
  assign bit_extender_4_out = {{8{1'b0}}, Instruction[7:0]};  // Bit_Extender bit_extender_4
  or or_1 (or_1_out, li, ori, ani, sli, sri);
  Shifter #(.width(16)) shifter_1 (.in(bit_extender_4_out), .\dist (4'b1000), .out(shifter_1_out));
  or or_2 (or_2_out, adi, sbi, blt, bge, bne, bnz, bez, beq);
  Multiplexer #(.select(3), .width(16)) multiplexer_1 (
    .in0(bit_extender_1_out), .in1(bit_extender_2_out), .in2(bit_extender_3_out), .in3(Instruction[15:0]),
    .in4(shifter_1_out), .out(imm), .sel(priority_encoder_1_out));  // open: in5, in6, in7, en
  Priority_Encoder priority_encoder_1 (
    .in0(or_1_out), .in1(or_2_out), .in2(or_3_out), .in3(or_4_out), .in4(lui), .out(priority_encoder_1_out));  // open: in5, in6, in7, en_in
  or or_3 (or_3_out, MemWrite, ld);
  or or_4 (or_4_out, j, call);
  Demultiplexer #(.select(5)) demultiplexer_1 (
    .out0(HALT), .out1(put), .out2(li), .out3(lui), .out4(ld), .out5(MemWrite), .out6(add), .out7(sub),
    .out8(\and ), .out9(\or ), .out10(\not ), .out11(shl), .out12(shr), .out13(adi), .out14(sbi),
    .out15(ani), .out16(ori), .out17(sli), .out18(sri), .out19(blt), .out20(bge), .out21(beq), .out22(bne),
    .out23(bez), .out24(bnz), .out25(jr), .out26(ret), .out27(KBRead), .out28(out), .in(not_1_out),
    .sel(Instruction[18:14]));  // open: out29, out30, out31, en
  // NOT_Gate not_1 has open pins: in=open, out=not_1_out
  Demultiplexer demultiplexer_2 (.out0(j), .out1(call), .in(Instruction[19]), .sel(Instruction[16]));  // open: en
  or or_5 (load, li, lui, ld);
  or or_6 (RegWrite, WrtFromALU, KBRead, load);
  or or_7 (I_type, li, ani, adi, sbi, sri, sli, ori, lui);
  or or_8 (or_8_out, \and , ani);
  or or_9 (or_9_out, \or , ori);
  or or_10 (or_10_out, li, lui);
  or or_11 (or_11_out, add, adi);
  or or_12 (or_12_out, sub, sbi);
  or or_13 (or_13_out, shl, sli);
  or or_14 (or_14_out, shr, sri);
  Comparator #(.width(16)) comparator_1 (.a({16{1'b0}}), .b(rs_out), .eq(_0));  // open: gt, lt
  Comparator #(.width(16)) comparator_2 (.a(rs_out), .b(rt_out), .eq(tunnel_t), .lt(tunnel));  // open: gt
  or or_15 (ALUSrc, MemWrite, ani, adi, sbi, sri, sli, ori, ld);
  and and_1 (and_1_out, beq, tunnel_t);
  and and_2 (and_2_out, bne, not_2_out);
  // NOT_Gate not_2 has open pins: in=open, out=not_2_out
  Priority_Encoder #(.select(2)) priority_encoder_2 (
    .in0(WrtFromALU), .in1(ld), .in2(or_10_out), .in3(KBRead), .out(RegDataSrc));  // open: gs, en_out, en_in
  or or_16 (WrtFromALU, or_11_out, or_12_out, or_8_out, or_9_out, \not , or_13_out, or_14_out);
  or or_17 (or_17_out, MemWrite, ld, or_11_out);
  and and_3 (and_3_out, bge, not_3_out);
  // NOT_Gate not_3 has open pins: in=open, out=not_3_out
  and and_4 (and_4_out, bez, _0);
  and and_5 (and_5_out, bnz, not_4_out);
  // NOT_Gate not_4 has open pins: in=open, out=not_4_out
  Priority_Encoder priority_encoder_3 (
    .in0(1'b1), .in1(or_17_out), .in2(or_12_out), .in3(or_8_out), .in4(or_9_out), .in5(\not ),
    .in6(or_13_out), .in7(or_14_out), .out(ALUOp));  // open: en_in, gs, en_out
  and and_6 (and_6_out, blt, tunnel);
  or or_18 (or_18_out, j, call);
  Priority_Encoder #(.select(4)) priority_encoder_4 (
    .in0(1'b1), .in1(and_6_out), .in2(and_3_out), .in3(and_1_out), .in4(and_2_out), .in5(and_4_out),
    .in6(and_5_out), .in7(jr), .in8(or_18_out), .in9(ret), .out(PCSrc));  // open: in10, in11, in12, in13, in14, in15, gs, en_out, en_in

  assign out_7 = Instruction[13:11];
  assign out_8 = Instruction[10:8];
  assign out_10 = Instruction[7:5];

  // Other names for the same wires on the sheet: in = KBRead; imm5[4:0] = Instruction[4:0];
  //   imm8[7:0] = Instruction[7:0]; imm16[15:0] = Instruction[15:0]; OPC[4:0] = Instruction[18:14];
  //   JOPC[2:0] = Instruction[18:16]; type = Instruction[19]; st = MemWrite

  // Notes on the sheet:
  //   Type
  //   Opcode
  //   Jopcode
  //   imm16
  //   imm8
  //   imm5
  //   rs
  //   rt
  //   rd
endmodule
